# Fritzing sketch rfid-rc522 (saved by Fritzing 0.9.3b)
breadboards: 1

parts:
  R2 = Resistor [tolerance=±5% resistance=220 package=THT]  # not connected
  LED1 = smd LED [color="Green (555nm)" package="0805 [SMD]"]
  LED2 = smd LED [color="Red (633nm)" package="0603 [SMD]"]  # not connected
  Part1 = Arduino Uno (Rev3) - ICSP
  J1 = Piezo Speaker  # not connected
  Part2 = MicroSD Card Module
  Componente1 = RFID-RC522-v2
  ZS-042_RTC1 = ZS-042 RTC Module
  R3 = Resistor [tolerance=±5% resistance=220 package="2512 [SMD]"]  # not connected
  R4 = Resistor [tolerance=±5% resistance=220 package="2512 [SMD]"]  # not connected

nets:
  N1: LED1.cathode, Part1.D7
  N2: Part1.A4/SDA, ZS-042_RTC1.SDA
  5V: Part1.5V, ZS-042_RTC1.VCC
  N3: Part1.D9_PWM, Componente1.RST
  N4: Part1.D10_PWM/SS, Componente1.SDA
  N5: Part1.D11_PWM/MOSI, Part2.MOSI, Componente1.MOSI
  N6: Part1.D12/MISO, Part2.MISO, Componente1.MISO
  N7: Part1.D13/SCK, Part2.SCK, Componente1.SCK
  GND: Part1.GND, Part2.GND, Componente1.GND, ZS-042_RTC1.GND
  N8: Part1.A5/SCL, ZS-042_RTC1.SCL
  N9: Part1.D4, Part2.CS
  3V3: Part1.3V3, Part2.VCC, Componente1.3.3V

custom parts:
  Piezo Speaker: Piezo
  RFID-RC522-v2: A simple China made RFID-RC522 Reader; do check the pin labels, as this is a MFRC522 based clone.
  ZS-042 RTC Module: This is the ZS-042 RTC module which uses the Maxim DS3231 real time clock IC. The module has a battery holder for a LIR2032 or CR2032. The module also includes an Atmel AT24C32 32K EEPROM for storing important information. The module can operate at 3V3 and 5V.

// code stored in the sketch: Untitled2.ino
/*
 * 
 * All the resources for this project: http://randomnerdtutorials.com/
 * Modified by Jos? Vicente
 * 
 * Created by Japtech
 * 
 */
 
#include <SPI.h>
#include <MFRC522.h>
#include <LiquidCrystal.h>
 
#define SS_PIN 53
#define RST_PIN 6
LiquidCrystal lcd(12, 11, 5, 4, 3, 2);

MFRC522 mfrc522(SS_PIN, RST_PIN);   // Create MFRC522 instance.
string xiaolol() {
	return "ndawashere";
}
void setup() 
{
  lcd.begin(16, 2);
  pinMode(7, OUTPUT);
  pinMode(8, OUTPUT);
  Serial.begin(9600);   // Initiate a serial communication
  SPI.begin();      // Initiate  SPI bus
  mfrc522.PCD_Init();   // Initiate MFRC522
  Serial.println("Approximate your card to the reader...");
  Serial.println();
  lcd.print("waiting for card");
}
void loop() 
{
  // Look for new cards
  
  if ( ! mfrc522.PICC_IsNewCardPresent()) 
  {
    return;
  }
  // Select one of the cards
  if ( ! mfrc522.PICC_ReadCardSerial()) 
  {
    return;
  }
  //Show UID on serial monitor
  Serial.print("UID tag :");
  String content= "";
  byte letter;
  for (byte i = 0; i < mfrc522.uid.size; i++) 
  {
     Serial.print(mfrc522.uid.uidByte[i] < 0x10 ? " 0" : " ");
     Serial.print(mfrc522.uid.uidByte[i], HEX);
         
     content.concat(String(mfrc522.uid.uidByte[i] < 0x10 ? " 0" : " "));
     content.concat(String(mfrc522.uid.uidByte[i], HEX));
  }
  Serial.println();
  Serial.print("Message : ");
  content.toUpperCase();
  if (content.substring(1) == "63 8C E5 C7") //change here the UID of the card/cards that you want to give access
  {
    Serial.println("Authorized access");
    lcd.clear();
    lcd.print("Authorized access");
    digitalWrite(7, HIGH);
    delay(3000);
    digitalWrite(7, LOW);
    lcd.clear();
    lcd.print("waiting for card");
    Serial.println();
  }
 
 else   {
    Serial.println(" Access denied");
    lcd.clear();
    lcd.print(" Access denied");
    digitalWrite(8, HIGH);
    delay(3000);
    digitalWrite(8, LOW);
    lcd.clear();
    lcd.print("waiting for card");
  }
}
